// Logisim project hw4_build_processor.circ as structural Verilog: 13 circuits, main circuit main
// oneBitAdd
module main (
  input  reset
);

  wire addiz, addz, andz, beqz, bgtorbeq_1_brtrue, bgtz, clk, jalz, jrz, jumpz, jz, kb, lwz,
       memory_latch_1_oe_latched, memory_latch_1_we_latched, nclk, orz, regWE, shleft, shright, slc_imm,
       slc_rt, subz, swz, tt, vd;
  wire [2:0] multiplexer_1_out, multiplexer_2_out;
  wire [3:0] opcode;
  wire [6:0] keyboard_1_data;
  wire [7:0] kbdata;
  wire [11:0] addr12, pc_1_data_out;
  wire [15:0] adder_2_result, alu_out, bit_extender_1_out, memory_latch_1_address_latched,
       memory_latch_1_data_in_latched, multiplexer_3_out, multiplexer_4_out, multiplexer_5_out,
       multiplexer_7_out, multiplexer_10_out, pc1, pc1JBr, r0, r1, ram_1_dout, regWD;
  wire [15:12] addr16;

  Clock clock_1 (.out(clk));
  PC pc_1 (.data_in(pc1JBr), .data_out({addr16, pc_1_data_out}), .reset(reset), .clk(clk), .reg_W_enab(1'b1));
  not not_1 (nclk, clk);
  ROM #(.addrWidth(16), .dataWidth(16)) rom_1 (.addr({addr16, pc_1_data_out}), .data({opcode, addr12}));
  adder adder_1 (.result(pc1), .B(16'h1), .A({addr16, pc_1_data_out}));  // open: Cin1, ovf
  or or_1 (regWE, kb, lwz, orz, andz, jalz, shleft, shright, subz, addz, addiz);
  Multiplexer #(.width(3), .enable("false")) multiplexer_1 (
    .in0(addr12[5:3]), .in1(addr12[8:6]), .out(multiplexer_1_out), .sel(slc_rt));
  or or_2 (jumpz, jz, jalz);
  RegisterFile registerfile_1 (
    .data_in(regWD), .rd(multiplexer_2_out), .write_enable(regWE), .reset(reset), .rs0(addr12[11:9]),
    .clk(nclk), .rs1(addr12[8:6]), .rs0_contents(r0), .rs1_contents(r1));
  Multiplexer #(.width(3), .enable("false")) multiplexer_2 (
    .in0(multiplexer_1_out), .in1(3'b111), .out(multiplexer_2_out), .sel(jalz));
  or or_3 (slc_rt, lwz, bgtz, beqz, addiz);
  Multiplexer #(.width(16), .enable("false")) multiplexer_3 (
    .in0(r1), .in1(bit_extender_1_out), .out(multiplexer_3_out), .sel(slc_imm));
  assign bit_extender_1_out = {{10{addr12[5]}}, addr12[5:0]};  // Bit_Extender bit_extender_1
  Decoder #(.select(4)) decoder_1 (
    .out0(tt), .out1(kb), .out2(lwz), .out3(swz), .out4(beqz), .out5(bgtz), .out6(orz), .out7(andz),
    .out8(addiz), .out9(addz), .out10(subz), .out11(shright), .out12(shleft), .out13(jz), .out14(jalz),
    .out15(jrz), .sel(opcode));  // open: en
  alu alu_1 (.A(r0), .B(multiplexer_3_out), .alu_result(alu_out), .opcode(opcode), .shamt(addr12[2:0]));
  memory_latch memory_latch_1 (
    .address(alu_out), .WE(swz), .clk(clk), .data_in(r1), .address_latched(memory_latch_1_address_latched),
    .WE_latched(memory_latch_1_we_latched), .OE_latched(memory_latch_1_oe_latched),
    .data_in_latched(memory_latch_1_data_in_latched));
  adder adder_2 (.result(adder_2_result), .B(bit_extender_1_out), .A(pc1));  // open: Cin1, ovf
  RAM #(.addrWidth(16), .dataWidth(16), .trigger("high"), .databus("bibus")) ram_1 (
    .addr(memory_latch_1_address_latched), .we(memory_latch_1_we_latched), .oe(memory_latch_1_oe_latched),
    .din(memory_latch_1_data_in_latched), .dout(ram_1_dout));
  Multiplexer #(.width(16), .enable("false")) multiplexer_4 (
    .in0(pc1), .in1(adder_2_result), .out(multiplexer_4_out), .sel(bgtorbeq_1_brtrue));
  bgtORbeq bgtorbeq_1 (.bgtz(bgtz), .beqz(beqz), .brtrue(bgtorbeq_1_brtrue), .alu_res(alu_out));
  Multiplexer #(.width(16), .enable("false")) multiplexer_5 (
    .in0(multiplexer_4_out), .in1({addr16, addr12}), .out(multiplexer_5_out), .sel(jumpz));
  or or_4 (slc_imm, swz, lwz, addiz);
  Multiplexer #(.width(16), .enable("false")) multiplexer_6 (
    .in0(multiplexer_5_out), .in1(r0), .out(pc1JBr), .sel(jrz));
  Multiplexer #(.width(16), .enable("false")) multiplexer_7 (
    .in0(alu_out), .in1(ram_1_dout), .out(multiplexer_7_out), .sel(lwz));
  Multiplexer #(.width(16), .enable("false")) multiplexer_8 (
    .in0(multiplexer_10_out), .in1({{8{1'b0}}, kbdata}), .out(regWD), .sel(kb));
  Keyboard keyboard_1 (.clk(clk), .re(kb), .clr(reset), .avail(vd), .data(keyboard_1_data));
  Multiplexer #(.enable("false")) multiplexer_9 (.in0(1'b1), .in1(1'b0), .out(kbdata[7]), .sel(vd));
  TTY #(.rows(13), .cols(80), .trigger("falling")) tty_1 (.data(r0[6:0]), .clk(clk), .we(tt), .clr(reset));
  Multiplexer #(.width(16), .enable("false")) multiplexer_10 (
    .in0(multiplexer_7_out), .in1(pc1), .out(multiplexer_10_out), .sel(jalz));
  Multiplexer #(.width(7), .enable("false")) multiplexer_11 (
    .in0({7{1'b0}}), .in1(keyboard_1_data), .out(kbdata[6:0]), .sel(vd));

  // Other names for the same wires on the sheet: addr16[11:0] = addr12; imm[5:0] = addr12[5:0];
  //   shamt[2:0] = addr12[2:0]; rd[2:0] = addr12[5:3]; rt[2:0] = addr12[8:6]; rs[2:0] = addr12[11:9];
  //   kbout[7:0] = kbdata; VKB[6:0] = kbdata[6:0]; vkb_t = kbdata[7]

  // Notes on the sheet:
  //   contents of rom_1 (hex, n*v repeats v):
  //   8100 8903 1008 82a0 400 893f 583b 403f
endmodule

module OneBitAdd (
  input  Cin,
  input  A,
  input  B,
  input  S,
  output sum,
  output Cout
);

  wire and_1_out, and_2_out, xor_1_out, xor_3_out;

  xor xor_1 (xor_1_out, B, S);
  and and_1 (and_1_out, xor_1_out, A);
  xor xor_2 (Cout, and_1_out, and_2_out);
  xor xor_3 (xor_3_out, A, xor_1_out);
  and and_2 (and_2_out, xor_3_out, Cin);
  xor xor_4 (sum, Cin, xor_3_out);
endmodule

module subtractor (
  input  Cin1,
  input  [15:0] B,
  input  [15:0] A,
  output [15:0] result,
  output ovf
);

  wire Cin7, Cin13, onebitadd_1_cout, onebitadd_2_cout, onebitadd_3_cout, onebitadd_4_cout, onebitadd_5_cout,
       onebitadd_6_cout, onebitadd_7_cout, onebitadd_8_cout, onebitadd_9_cout, onebitadd_11_cout,
       onebitadd_12_cout, onebitadd_13_cout, onebitadd_14_cout, onebitadd_15_cout, xor_1_out;

  OneBitAdd onebitadd_1 (.A(A[12]), .B(B[12]), .S(1'b1), .sum(result[12]), .Cin(Cin13), .Cout(onebitadd_1_cout));
  OneBitAdd onebitadd_2 (
    .A(A[13]), .B(B[13]), .S(1'b1), .sum(result[13]), .Cin(onebitadd_1_cout), .Cout(onebitadd_2_cout));
  OneBitAdd onebitadd_3 (
    .A(A[14]), .B(B[14]), .S(1'b1), .sum(result[14]), .Cin(onebitadd_2_cout), .Cout(onebitadd_3_cout));
  OneBitAdd onebitadd_4 (
    .A(A[15]), .B(B[15]), .S(1'b1), .sum(result[15]), .Cin(onebitadd_3_cout), .Cout(onebitadd_4_cout));
  xor xor_1 (xor_1_out, 1'b1, Cin1);
  OneBitAdd onebitadd_5 (.A(A[6]), .B(B[6]), .S(1'b1), .sum(result[6]), .Cin(Cin7), .Cout(onebitadd_5_cout));
  OneBitAdd onebitadd_6 (
    .A(A[7]), .B(B[7]), .S(1'b1), .sum(result[7]), .Cin(onebitadd_5_cout), .Cout(onebitadd_6_cout));
  OneBitAdd onebitadd_7 (
    .A(A[8]), .B(B[8]), .S(1'b1), .sum(result[8]), .Cin(onebitadd_6_cout), .Cout(onebitadd_7_cout));
  OneBitAdd onebitadd_8 (
    .A(A[9]), .B(B[9]), .S(1'b1), .sum(result[9]), .Cin(onebitadd_7_cout), .Cout(onebitadd_8_cout));
  OneBitAdd onebitadd_9 (
    .A(A[10]), .B(B[10]), .S(1'b1), .sum(result[10]), .Cin(onebitadd_8_cout), .Cout(onebitadd_9_cout));
  OneBitAdd onebitadd_10 (.A(A[11]), .B(B[11]), .S(1'b1), .sum(result[11]), .Cin(onebitadd_9_cout), .Cout(Cin13));
  xor xor_2 (ovf, onebitadd_3_cout, onebitadd_4_cout);
  OneBitAdd onebitadd_11 (.A(A[0]), .B(B[0]), .S(1'b1), .sum(result[0]), .Cin(xor_1_out), .Cout(onebitadd_11_cout));
  OneBitAdd onebitadd_12 (
    .A(A[1]), .B(B[1]), .S(1'b1), .sum(result[1]), .Cin(onebitadd_11_cout), .Cout(onebitadd_12_cout));
  OneBitAdd onebitadd_13 (
    .A(A[2]), .B(B[2]), .S(1'b1), .sum(result[2]), .Cin(onebitadd_12_cout), .Cout(onebitadd_13_cout));
  OneBitAdd onebitadd_14 (
    .A(A[3]), .B(B[3]), .S(1'b1), .sum(result[3]), .Cin(onebitadd_13_cout), .Cout(onebitadd_14_cout));
  OneBitAdd onebitadd_15 (
    .A(A[4]), .B(B[4]), .S(1'b1), .sum(result[4]), .Cin(onebitadd_14_cout), .Cout(onebitadd_15_cout));
  OneBitAdd onebitadd_16 (.A(A[5]), .B(B[5]), .S(1'b1), .sum(result[5]), .Cin(onebitadd_15_cout), .Cout(Cin7));

  // Other names for the same wires on the sheet: A1 = A[0]; A2 = A[1]; A3 = A[2]; A4 = A[3]; A5 = A[4]; A6 = A[5];
  //   A7 = A[6]; A8 = A[7]; A9 = A[8]; A10 = A[9]; A11 = A[10]; A12 = A[11]; A13 = A[12]; A14 = A[13]; A15 = A[14];
  //   A16 = A[15]; B1 = B[0]; B2 = B[1]; B3 = B[2]; B4 = B[3]; B5 = B[4]; B6 = B[5]; B7 = B[6]; B8 = B[7]; B9 = B[8];
  //   B10 = B[9]; B11 = B[10]; B12 = B[11]; B13 = B[12]; B14 = B[13]; B15 = B[14]; B16 = B[15]; o1 = result[0];
  //   o2 = result[1]; o3 = result[2]; o4 = result[3]; o5 = result[4]; o6 = result[5]; o7 = result[6]; o8 = result[7];
  //   o9 = result[8]; o10 = result[9]; o11 = result[10]; o12 = result[11]; o13 = result[12]; o14 = result[13];
  //   o15 = result[14]; o16 = result[15]
endmodule

module adder (
  input  Cin1,
  input  [15:0] B,
  input  [15:0] A,
  output [15:0] result,
  output ovf
);

  wire Cin7, Cin13, onebitadd_1_cout, onebitadd_2_cout, onebitadd_3_cout, onebitadd_4_cout, onebitadd_5_cout,
       onebitadd_6_cout, onebitadd_7_cout, onebitadd_8_cout, onebitadd_9_cout, onebitadd_11_cout,
       onebitadd_12_cout, onebitadd_13_cout, onebitadd_14_cout, onebitadd_15_cout, xor_1_out;

  OneBitAdd onebitadd_1 (.A(A[12]), .B(B[12]), .S(1'b0), .sum(result[12]), .Cin(Cin13), .Cout(onebitadd_1_cout));
  OneBitAdd onebitadd_2 (
    .A(A[13]), .B(B[13]), .S(1'b0), .sum(result[13]), .Cin(onebitadd_1_cout), .Cout(onebitadd_2_cout));
  OneBitAdd onebitadd_3 (
    .A(A[14]), .B(B[14]), .S(1'b0), .sum(result[14]), .Cin(onebitadd_2_cout), .Cout(onebitadd_3_cout));
  OneBitAdd onebitadd_4 (
    .A(A[15]), .B(B[15]), .S(1'b0), .sum(result[15]), .Cin(onebitadd_3_cout), .Cout(onebitadd_4_cout));
  xor xor_1 (xor_1_out, 1'b0, Cin1);
  OneBitAdd onebitadd_5 (.A(A[6]), .B(B[6]), .S(1'b0), .sum(result[6]), .Cin(Cin7), .Cout(onebitadd_5_cout));
  OneBitAdd onebitadd_6 (
    .A(A[7]), .B(B[7]), .S(1'b0), .sum(result[7]), .Cin(onebitadd_5_cout), .Cout(onebitadd_6_cout));
  OneBitAdd onebitadd_7 (
    .A(A[8]), .B(B[8]), .S(1'b0), .sum(result[8]), .Cin(onebitadd_6_cout), .Cout(onebitadd_7_cout));
  OneBitAdd onebitadd_8 (
    .A(A[9]), .B(B[9]), .S(1'b0), .sum(result[9]), .Cin(onebitadd_7_cout), .Cout(onebitadd_8_cout));
  OneBitAdd onebitadd_9 (
    .A(A[10]), .B(B[10]), .S(1'b0), .sum(result[10]), .Cin(onebitadd_8_cout), .Cout(onebitadd_9_cout));
  OneBitAdd onebitadd_10 (.A(A[11]), .B(B[11]), .S(1'b0), .sum(result[11]), .Cin(onebitadd_9_cout), .Cout(Cin13));
  xor xor_2 (ovf, onebitadd_3_cout, onebitadd_4_cout);
  OneBitAdd onebitadd_11 (.A(A[0]), .B(B[0]), .S(1'b0), .sum(result[0]), .Cin(xor_1_out), .Cout(onebitadd_11_cout));
  OneBitAdd onebitadd_12 (
    .A(A[1]), .B(B[1]), .S(1'b0), .sum(result[1]), .Cin(onebitadd_11_cout), .Cout(onebitadd_12_cout));
  OneBitAdd onebitadd_13 (
    .A(A[2]), .B(B[2]), .S(1'b0), .sum(result[2]), .Cin(onebitadd_12_cout), .Cout(onebitadd_13_cout));
  OneBitAdd onebitadd_14 (
    .A(A[3]), .B(B[3]), .S(1'b0), .sum(result[3]), .Cin(onebitadd_13_cout), .Cout(onebitadd_14_cout));
  OneBitAdd onebitadd_15 (
    .A(A[4]), .B(B[4]), .S(1'b0), .sum(result[4]), .Cin(onebitadd_14_cout), .Cout(onebitadd_15_cout));
  OneBitAdd onebitadd_16 (.A(A[5]), .B(B[5]), .S(1'b0), .sum(result[5]), .Cin(onebitadd_15_cout), .Cout(Cin7));

  // Other names for the same wires on the sheet: A1 = A[0]; A2 = A[1]; A3 = A[2]; A4 = A[3]; A5 = A[4]; A6 = A[5];
  //   A7 = A[6]; A8 = A[7]; A9 = A[8]; A10 = A[9]; A11 = A[10]; A12 = A[11]; A13 = A[12]; A14 = A[13]; A15 = A[14];
  //   A16 = A[15]; B1 = B[0]; B2 = B[1]; B3 = B[2]; B4 = B[3]; B5 = B[4]; B6 = B[5]; B7 = B[6]; B8 = B[7]; B9 = B[8];
  //   B10 = B[9]; B11 = B[10]; B12 = B[11]; B13 = B[12]; B14 = B[13]; B15 = B[14]; B16 = B[15]; o1 = result[0];
  //   o2 = result[1]; o3 = result[2]; o4 = result[3]; o5 = result[4]; o6 = result[5]; o7 = result[6]; o8 = result[7];
  //   o9 = result[8]; o10 = result[9]; o11 = result[10]; o12 = result[11]; o13 = result[12]; o14 = result[13];
  //   o15 = result[14]; o16 = result[15]
endmodule

module alu (
  input  [15:0] A,
  input  [15:0] B,
  input  [3:0] opcode,
  input  [2:0] shamt,
  output [15:0] alu_result
);

  wire adder_1_ovf;
  wire [15:0] add, \and , \or , shleft, shright, sub;

  adder adder_1 (.result(add), .B(B), .A(A), .ovf(adder_1_ovf));  // open: Cin1
  subtractor subtractor_1 (.result(sub), .B(B), .A(A));  // open: Cin1, ovf
  assign \and  = A & B;  // AND_Gate and_1, 16 bits wide
  assign \or  = A | B;  // OR_Gate or_1, 16 bits wide
  shR shr_1 (.data_in(A), .shamt(shamt), .data_out(shright));
  shL shl_1 (.data_in(A), .shamt(shamt), .data_out(shleft));
  Multiplexer #(.select(4), .width(16), .enable("false")) multiplexer_1 (
    .in0({16{1'b0}}), .in1({16{1'b0}}), .in2(add), .in3(add), .in4(sub), .in5(sub), .in6(\or ), .in7(\and ),
    .in8(add), .in9(add), .in10(sub), .in11(shright), .in12(shleft), .in13({16{1'b0}}), .in14({16{1'b0}}),
    .in15({16{1'b0}}), .out(alu_result), .sel(opcode));

  // Other names for the same wires on the sheet: A_val[15:0] = A
endmodule

module PC (
  input  [15:0] data_in,
  input  reset,
  input  clk,
  input  reg_W_enab,
  output [15:0] data_out
);

  wire reg_W_enab_t;

  and and_1 (reg_W_enab_t, clk, reg_W_enab);
  D_Flip_Flop d_ff_1 (.D(data_in[0]), .clk(reg_W_enab_t), .Q(data_out[0]), .reset(reset));  // open: Qn, preset
  D_Flip_Flop d_ff_2 (.D(data_in[1]), .clk(reg_W_enab_t), .Q(data_out[1]), .reset(reset));  // open: Qn, preset
  D_Flip_Flop d_ff_3 (.D(data_in[2]), .clk(reg_W_enab_t), .Q(data_out[2]), .reset(reset));  // open: Qn, preset
  D_Flip_Flop d_ff_4 (.D(data_in[3]), .clk(reg_W_enab_t), .Q(data_out[3]), .reset(reset));  // open: Qn, preset
  D_Flip_Flop d_ff_5 (.D(data_in[4]), .clk(reg_W_enab_t), .Q(data_out[4]), .reset(reset));  // open: Qn, preset
  D_Flip_Flop d_ff_6 (.D(data_in[5]), .clk(reg_W_enab_t), .Q(data_out[5]), .reset(reset));  // open: Qn, preset
  D_Flip_Flop d_ff_7 (.D(data_in[6]), .clk(reg_W_enab_t), .Q(data_out[6]), .reset(reset));  // open: Qn, preset
  D_Flip_Flop d_ff_8 (.D(data_in[7]), .clk(reg_W_enab_t), .Q(data_out[7]), .reset(reset));  // open: Qn, preset
  D_Flip_Flop d_ff_9 (.D(data_in[8]), .clk(reg_W_enab_t), .Q(data_out[8]), .reset(reset));  // open: Qn, preset
  D_Flip_Flop d_ff_10 (.D(data_in[9]), .clk(reg_W_enab_t), .Q(data_out[9]), .reset(reset));  // open: Qn, preset
  D_Flip_Flop d_ff_11 (.D(data_in[10]), .clk(reg_W_enab_t), .Q(data_out[10]), .reset(reset));  // open: Qn, preset
  D_Flip_Flop d_ff_12 (.D(data_in[11]), .clk(reg_W_enab_t), .Q(data_out[11]), .reset(reset));  // open: Qn, preset
  D_Flip_Flop d_ff_13 (.D(data_in[12]), .clk(reg_W_enab_t), .Q(data_out[12]), .reset(reset));  // open: Qn, preset
  D_Flip_Flop d_ff_14 (.D(data_in[13]), .clk(reg_W_enab_t), .Q(data_out[13]), .reset(reset));  // open: Qn, preset
  D_Flip_Flop d_ff_15 (.D(data_in[14]), .clk(reg_W_enab_t), .Q(data_out[14]), .reset(reset));  // open: Qn, preset
  D_Flip_Flop d_ff_16 (.D(data_in[15]), .clk(reg_W_enab_t), .Q(data_out[15]), .reset(reset));  // open: Qn, preset

  // Other names for the same wires on the sheet: d0 = data_in[0]; d1 = data_in[1]; d2 = data_in[2]; d3 = data_in[3];
  //   d4 = data_in[4]; d5 = data_in[5]; d6 = data_in[6]; d7 = data_in[7]; d8 = data_in[8]; d9 = data_in[9];
  //   d10 = data_in[10]; d11 = data_in[11]; d12 = data_in[12]; d13 = data_in[13]; d14 = data_in[14];
  //   d15 = data_in[15]; q0 = data_out[0]; q1 = data_out[1]; q2 = data_out[2]; q3 = data_out[3]; q4 = data_out[4];
  //   q5 = data_out[5]; q6 = data_out[6]; q7 = data_out[7]; q8 = data_out[8]; q9 = data_out[9]; q10 = data_out[10];
  //   q11 = data_out[11]; q12 = data_out[12]; q13 = data_out[13]; q14 = data_out[14]; q15 = data_out[15]; r = reset
endmodule

module register (
  input  [15:0] data_in,
  input  reset,
  input  clk,
  input  reg_W_enab,
  output [15:0] data_out
);

  wire reg_W_enab_t;

  and and_1 (reg_W_enab_t, clk, reg_W_enab);
  D_Flip_Flop d_ff_1 (.D(data_in[0]), .clk(reg_W_enab_t), .Q(data_out[0]), .reset(reset));  // open: Qn, preset
  D_Flip_Flop d_ff_2 (.D(data_in[1]), .clk(reg_W_enab_t), .Q(data_out[1]), .reset(reset));  // open: Qn, preset
  D_Flip_Flop d_ff_3 (.D(data_in[2]), .clk(reg_W_enab_t), .Q(data_out[2]), .reset(reset));  // open: Qn, preset
  D_Flip_Flop d_ff_4 (.D(data_in[3]), .clk(reg_W_enab_t), .Q(data_out[3]), .reset(reset));  // open: Qn, preset
  D_Flip_Flop d_ff_5 (.D(data_in[4]), .clk(reg_W_enab_t), .Q(data_out[4]), .reset(reset));  // open: Qn, preset
  D_Flip_Flop d_ff_6 (.D(data_in[5]), .clk(reg_W_enab_t), .Q(data_out[5]), .reset(reset));  // open: Qn, preset
  D_Flip_Flop d_ff_7 (.D(data_in[6]), .clk(reg_W_enab_t), .Q(data_out[6]), .reset(reset));  // open: Qn, preset
  D_Flip_Flop d_ff_8 (.D(data_in[7]), .clk(reg_W_enab_t), .Q(data_out[7]), .reset(reset));  // open: Qn, preset
  D_Flip_Flop d_ff_9 (.D(data_in[8]), .clk(reg_W_enab_t), .Q(data_out[8]), .reset(reset));  // open: Qn, preset
  D_Flip_Flop d_ff_10 (.D(data_in[9]), .clk(reg_W_enab_t), .Q(data_out[9]), .reset(reset));  // open: Qn, preset
  D_Flip_Flop d_ff_11 (.D(data_in[10]), .clk(reg_W_enab_t), .Q(data_out[10]), .reset(reset));  // open: Qn, preset
  D_Flip_Flop d_ff_12 (.D(data_in[11]), .clk(reg_W_enab_t), .Q(data_out[11]), .reset(reset));  // open: Qn, preset
  D_Flip_Flop d_ff_13 (.D(data_in[12]), .clk(reg_W_enab_t), .Q(data_out[12]), .reset(reset));  // open: Qn, preset
  D_Flip_Flop d_ff_14 (.D(data_in[13]), .clk(reg_W_enab_t), .Q(data_out[13]), .reset(reset));  // open: Qn, preset
  D_Flip_Flop d_ff_15 (.D(data_in[14]), .clk(reg_W_enab_t), .Q(data_out[14]), .reset(reset));  // open: Qn, preset
  D_Flip_Flop d_ff_16 (.D(data_in[15]), .clk(reg_W_enab_t), .Q(data_out[15]), .reset(reset));  // open: Qn, preset

  // Other names for the same wires on the sheet: d0 = data_in[0]; d1 = data_in[1]; d2 = data_in[2]; d3 = data_in[3];
  //   d4 = data_in[4]; d5 = data_in[5]; d6 = data_in[6]; d7 = data_in[7]; d8 = data_in[8]; d9 = data_in[9];
  //   d10 = data_in[10]; d11 = data_in[11]; d12 = data_in[12]; d13 = data_in[13]; d14 = data_in[14];
  //   d15 = data_in[15]; q0 = data_out[0]; q1 = data_out[1]; q2 = data_out[2]; q3 = data_out[3]; q4 = data_out[4];
  //   q5 = data_out[5]; q6 = data_out[6]; q7 = data_out[7]; q8 = data_out[8]; q9 = data_out[9]; q10 = data_out[10];
  //   q11 = data_out[11]; q12 = data_out[12]; q13 = data_out[13]; q14 = data_out[14]; q15 = data_out[15]; r = reset
endmodule

module memory_latch (
  input  [15:0] address,
  input  WE,
  input  clk,
  input  [15:0] data_in,
  output [15:0] address_latched,
  output WE_latched,
  output OE_latched,
  output [15:0] data_in_latched
);

  wire d_ff_1_q;
  wire [15:0] register_1_q;

  Register #(.width(16), .trigger("falling")) register_1 (
    .D(address), .en(WE), .clk(clk), .Q(register_1_q));  // open: clr
  D_Flip_Flop #(.trigger("falling")) d_ff_1 (.D(WE), .clk(clk), .Q(d_ff_1_q));  // open: Qn, preset, reset
  Register #(.width(16), .trigger("falling")) register_2 (
    .D(data_in), .en(WE), .clk(clk), .Q(data_in_latched));  // open: clr
  Multiplexer #(.width(16), .enable("false")) multiplexer_1 (
    .in0(address), .in1(register_1_q), .out(address_latched), .sel(d_ff_1_q));
  and and_1 (WE_latched, clk, d_ff_1_q);
  not not_1 (OE_latched, WE_latched);
endmodule

module shR (
  input  [15:0] data_in,
  input  [2:0] shamt,
  output [15:0] data_out
);

  wire [15:0] multiplexer_1_out, multiplexer_2_out;

  Multiplexer #(.width(16), .enable("false")) multiplexer_1 (
    .in0(data_in), .in1({{2{data_in[15]}}, data_in[14:1]}), .out(multiplexer_1_out), .sel(shamt[0]));
  Multiplexer #(.width(16), .enable("false")) multiplexer_2 (
    .in0(multiplexer_1_out), .in1({{3{multiplexer_1_out[15]}}, multiplexer_1_out[14:2]}),
    .out(multiplexer_2_out), .sel(shamt[1]));
  Multiplexer #(.width(16), .enable("false")) multiplexer_3 (
    .in0(multiplexer_2_out), .in1({{5{multiplexer_2_out[15]}}, multiplexer_2_out[14:4]}), .out(data_out),
    .sel(shamt[2]));

  // Other names for the same wires on the sheet: sh0 = shamt[0]; sh1 = shamt[1]; sh2 = shamt[2]
endmodule

module shL (
  input  [15:0] data_in,
  input  [2:0] shamt,
  output [15:0] data_out
);

  wire [15:0] multiplexer_1_out, multiplexer_2_out;

  Multiplexer #(.width(16), .enable("false")) multiplexer_1 (
    .in0(data_in), .in1({data_in[14:0], 1'b0}), .out(multiplexer_1_out), .sel(shamt[0]));
  Multiplexer #(.width(16), .enable("false")) multiplexer_2 (
    .in0(multiplexer_1_out), .in1({multiplexer_1_out[13:0], 2'b00}), .out(multiplexer_2_out), .sel(shamt[1]));
  Multiplexer #(.width(16), .enable("false")) multiplexer_3 (
    .in0(multiplexer_2_out), .in1({multiplexer_2_out[11:0], 4'b0000}), .out(data_out), .sel(shamt[2]));

  // Other names for the same wires on the sheet: sh0 = shamt[0]; sh1 = shamt[1]; sh2 = shamt[2]
endmodule

module bgt (
  input  [15:0] alu_res,
  output out_2
);

  wire and_1_out, nor_1_out, or_1_out;

  nor nor_1 (nor_1_out, alu_res[0], alu_res[1], alu_res[2], alu_res[3], alu_res[4], alu_res[5], alu_res[6], alu_res[7], alu_res[8], alu_res[9], alu_res[10], alu_res[11], alu_res[12], alu_res[13], alu_res[14], alu_res[15]);
  and and_1 (and_1_out, alu_res[15], 1'b1);
  or or_1 (or_1_out, nor_1_out, and_1_out);
  not not_1 (out_2, or_1_out);
endmodule

module RegisterFile (
  input  [15:0] data_in,
  input  [2:0] rd,
  input  write_enable,
  input  reset,
  input  [2:0] rs0,
  input  clk,
  input  [2:0] rs1,
  output [15:0] rs0_contents,
  output [15:0] rs1_contents
);

  wire decoder_1_out1, decoder_1_out2, decoder_1_out3, decoder_1_out4, decoder_1_out5, decoder_1_out6,
       decoder_1_out7;
  wire [15:0] reg1, reg2, reg3, reg4, reg5, reg6, reg7;

  Decoder #(.select(3)) decoder_1 (
    .out1(decoder_1_out1), .out2(decoder_1_out2), .out3(decoder_1_out3), .out4(decoder_1_out4),
    .out5(decoder_1_out5), .out6(decoder_1_out6), .out7(decoder_1_out7), .sel(rd), .en(write_enable));  // open: out0
  register register_1 (.data_in(data_in), .data_out(reg1), .reset(reset), .clk(clk), .reg_W_enab(decoder_1_out1));
  register register_2 (.data_in(data_in), .data_out(reg2), .reset(reset), .clk(clk), .reg_W_enab(decoder_1_out2));
  register register_3 (.data_in(data_in), .data_out(reg3), .reset(reset), .clk(clk), .reg_W_enab(decoder_1_out3));
  // Probe on reg3
  register register_4 (.data_in(data_in), .data_out(reg4), .reset(reset), .clk(clk), .reg_W_enab(decoder_1_out4));
  register register_5 (.data_in(data_in), .data_out(reg6), .reset(reset), .clk(clk), .reg_W_enab(decoder_1_out6));
  register register_6 (.data_in(data_in), .data_out(reg7), .reset(reset), .clk(clk), .reg_W_enab(decoder_1_out7));
  // Probe on reg4
  // Probe on reg5
  register register_7 (.data_in(data_in), .data_out(reg5), .reset(reset), .clk(clk), .reg_W_enab(decoder_1_out5));
  // Probe on reg6
  // Probe on reg7
  // Probe on {16{1'b0}}
  // Probe on reg2
  Multiplexer #(.select(3), .width(16), .enable("false")) multiplexer_1 (
    .in0({16{1'b0}}), .in1(reg1), .in2(reg2), .in3(reg3), .in4(reg4), .in5(reg5), .in6(reg6), .in7(reg7),
    .out(rs0_contents), .sel(rs0));
  // Probe on reg1
  Multiplexer #(.select(3), .width(16), .enable("false")) multiplexer_2 (
    .in0({16{1'b0}}), .in1(reg1), .in2(reg2), .in3(reg3), .in4(reg4), .in5(reg5), .in6(reg6), .in7(reg7),
    .out(rs1_contents), .sel(rs1));
endmodule

module bgtORbeq (
  input  bgtz,
  input  [15:0] alu_res,
  input  beqz,
  output brtrue
);

  wire and_1_out, and_2_out, bgt_1_out_2, nor_1_out;

  bgt bgt_1 (.alu_res(alu_res), .out_2(bgt_1_out_2));
  nor nor_1 (nor_1_out, alu_res[0], alu_res[1], alu_res[2], alu_res[3], alu_res[4], alu_res[5], alu_res[6], alu_res[7], alu_res[8], alu_res[9], alu_res[10], alu_res[11], alu_res[12], alu_res[13], alu_res[14], alu_res[15]);
  and and_1 (and_1_out, bgt_1_out_2, bgtz);
  and and_2 (and_2_out, beqz, nor_1_out);
  or or_1 (brtrue, and_1_out, and_2_out);

  // Other names for the same wires on the sheet: alu_result[15:0] = alu_res
endmodule
